# Fritzing sketch Autometer (saved by Fritzing 0.9.2b)
circuit board: 8.46667cm x 5.64444cm
perfboards: 1

parts:
  JP4 = M16 [package=1x16_machine-pin-header_lock.004]
  JP5 = M16 [package=1x16_machine-pin-header_lock.004]
  Part1 = Arduino Micro (Rev3)

nets:
  N1: JP4.3, Part1.D4_PWM/A6
  N2: JP4.4, Part1.D5_PWM
  N3: JP4.5, Part1.A5
  N4: JP4.6, Part1.A4
  N5: JP4.10, Part1.VIN
  N6: JP4.11, Part1.A2
  N7: JP4.12, Part1.A1
  N8: JP4.13, Part1.A0
  N9: JP5.3, Part1.D1/TX
  N10: JP5.4, Part1.D0/RX
  N11: JP5.6, Part1.D2/SDA
  N12: JP5.7, Part1.D3/SCL
  N13: JP5.10, Part1.GND
  N14: JP5.11, Part1.D7
  N15: JP5.12, Part1.D8_PWM/A8
  N16: JP5.13, Part1.D9_PWM/A9
  N17: JP5.14, Part1.D10_PWM/A10
  N18: JP5.15, Part1.D11_PWM
  N19: JP5.16, Part1.D12_PWM/A11
